# Fritzing sketch touch (saved by Fritzing 0.9.3b)

parts:
  X1 = USB Connectors [package=usb-mb-h]
  S1 = Toggle Switch [package=THT]
  S2 = Toggle Switch [package=THT]
  DFPlayer_Mini1 = DFPlayer MINI [package="DIP (Dual Inline) [THT]"]
  SP1 = SPEAKER [package=pcb_mount_speaker]
  Part1 = Arduino Uno (Rev3) - ICSP
  R5 = Resistor [tolerance=±5% resistance=10k package=THT]
  R6 = Resistor [tolerance=±5% resistance=10k package=THT]
  R8 = Resistor [tolerance=±5% resistance=10k package=THT]
  R9 = Resistor [tolerance=±5% resistance=10k package=THT]  # not connected
  R10 = Resistor [tolerance=±5% resistance=10k package=THT]  # not connected
  R11 = Resistor [tolerance=±5% resistance=10k package=THT]
  D2 = Rectifier Diode [part_number=1N4001 package="300 mil [THT]"]
  D3 = Rectifier Diode [part_number=1N4001 package="300 mil [THT]"]
  JP1 = Header 1 [package=snap-male]
  JP2 = Header 1 [package=snap-male]
  JP3 = Header 1 [package=snap-male]
  JP4 = Header 1 [package=snap-male]
  R13 = Resistor [tolerance=±5% resistance=10k package=THT]
  R12 = Resistor [tolerance=±5% resistance=10k package=THT]

nets:
  N1: X1.D+, S1.L1
  N2: X1.D-, S2.L2
  N3: X1.GND, DFPlayer_Mini1.GND#9
  N4: S1.COM, DFPlayer_Mini1.USB_+
  N5: S2.COM, DFPlayer_Mini1.USB_-
  N6: DFPlayer_Mini1.RX, R6.Pin_0
  N7: DFPlayer_Mini1.TX, R5.Pin_1
  N8: DFPlayer_Mini1.SPK1, SP1.+
  N9: DFPlayer_Mini1.GND#6, Part1.GND
  N10: DFPlayer_Mini1.SPK2, SP1.-
  N11: Part1.D8, JP1.1, R13.Pin_0
  N12: Part1.D9_PWM, JP3.1, R12.Pin_0
  N13: Part1.D0/RX, R5.Pin_0
  N14: Part1.D1/TX, R6.Pin_1
  N15: Part1.D3_PWM, R8.Pin_1
  N16: Part1.D5_PWM, R11.Pin_1
  N17: D2.cathode, JP4.1
  N18: D3.cathode, JP2.1

custom parts:
  DFPlayer MINI: MP3 module by DFRobot.com for playing Music from an SD-Card. Supports WAV and MP3 files.
